// Logisim project Traffic signals.circ as structural Verilog: 1 circuit, main circuit main
module main (
  input  A,
  input  B,
  output GA,
  output GB
);

  wire not_1_out;

  not not_1 (not_1_out, A);
  and and_1 (GB, not_1_out, B);

  assign GA = A;
endmodule
